# Fritzing sketch circuit (saved by Fritzing 0.9.10b)

parts:
  Part1 = Arduino Uno (Rev3)
  LCM1602_IIC1 = LCM1602 IIC [part_number="LCM1602 IIC" chip_label="LCM1602 IIC" package="DIP (Dual Inline) [THT]"]
  LCD1 = LCD screen
  Part2 = Black Joystick KY-023

nets:
  N1: Part1.A1, Part2.VRx
  N2: Part1.A4/SDA, LCM1602_IIC1.SDA
  N3: Part1.A5/SCL, LCM1602_IIC1.SCL
  N4: Part1.D2, Part2.SW
  5V: Part1.5V, LCM1602_IIC1.VCC
  GND: Part1.GND, LCM1602_IIC1.GND, Part2.GND
  VSS: LCM1602_IIC1.VSS, LCD1.VSS
  VDD: LCM1602_IIC1.VDD, LCD1.VDD
  N5: LCM1602_IIC1.V0, LCD1.V0
  N6: LCM1602_IIC1.RS, LCD1.RS
  N7: LCM1602_IIC1.RW, LCD1.R/W
  N8: LCM1602_IIC1.E, LCD1.E
  N9: LCM1602_IIC1.D0, LCD1.DB0
  N10: LCM1602_IIC1.D1, LCD1.DB1
  N11: LCM1602_IIC1.D2, LCD1.DB2
  N12: LCM1602_IIC1.D3, LCD1.DB3
  N13: LCM1602_IIC1.D4, LCD1.DB4
  N14: LCM1602_IIC1.D5, LCD1.DB5
  N15: LCM1602_IIC1.D6, LCD1.DB6
  N16: LCM1602_IIC1.D7, LCD1.DB7
  N17: LCM1602_IIC1.A, LCD1.LED+
  N18: LCM1602_IIC1.K, LCD1.LED-
  N19: LCM1602_IIC1.LED_A, LCM1602_IIC1.LED_B

custom parts:
  LCM1602 IIC: I2C-Module to use a 1602 or 2004 LCD on with the wire.h libory Serial LCD Modul
  Black Joystick KY-023: Description: The joystick is a combination of 2 analoog potentiometer and a digital switch. Arduino GND --> Module pin - Arduino +5V --> Module pin +5V Arduino Analoog 0 --> Module VRx Arduino Analoog 1 --> Module VRy Arduino Digital --> Module SW Dimensions: 1" x 1.25"
